# Fritzing sketch test_rtc-DS1302 (saved by Fritzing 0.9.3b)
breadboards: 1
stripboards: 4

parts:
  MH-Real-Time_Clock_Module_2 = RTC_DS1302_module  # not connected
  Част1 = Arduino Nano (Rev3.0)
  U1 = 74HC595 SMD [package="SO16 [SMD]"]
  LED1 = 7-SEGMENT-4DIGIT-YOUNGSUN [package=7-segment-4digit-youngsun]
  R1 = Resistor [tolerance=±5% resistance=220 package=THT]
  R2 = Resistor [tolerance=±5% resistance=220 package=THT]
  R3 = Resistor [tolerance=±5% resistance=220 package=THT]

nets:
  N1: Част1.D4, U1.DS
  N2: Част1.D5, U1.ST_CP
  N3: Част1.D6, U1.SH_CP
  N4: Част1.D11/MOSI, R3.Pin_0
  N5: Част1.D12/MISO, R2.Pin_0
  N6: U1.MR, U1.VCC
  N7: U1.Q0, LED1.G
  N8: LED1.DIG3, R1.Pin_1
  N9: LED1.C, R3.Pin_1
  N10: LED1.B, R2.Pin_1

custom parts:
  RTC_DS1302_module: Arduino module DS1302 SPI Real Time Clock
